// Logisim project EP2.circ as structural Verilog: 6 circuits, main circuit ula
module main (
  input  OP,
  input  [7:0] A,
  input  [7:0] B,
  output [7:0] R,
  output o1,
  output o2,
  output o3,
  output o4,
  output o5,
  output o6,
  output o7,
  output o8
);

  ula ula_1 (.OP(OP), .A(A), .B(B), .R(R), .o1(o1), .o2(o2), .c0(o3), .c1(o4), .c2(o5), .c3(o6), .c4(o7), .c5(o8));

  // Notes on the sheet:
  //   06/2022
  //   ULA - unidade logico aritmetica
  //   EP2 - MAC0329: Algebra Booleana e Aplicacoes
  //   Adriano Elias Andrade e Otavio de Oliveira Silva
endmodule

module ula (
  input  OP,
  input  [7:0] A,
  input  [7:0] B,
  output [7:0] R,
  output o1,
  output o2,
  output c0,
  output c1,
  output c2,
  output c3,
  output c4,
  output c5
);

  somador somador_1 (.OP(OP), .A(A), .B(B), .S(R), .CS(o2), .SS(o1));
  comparador comparador_1 (.A(A), .B(B), .c0(c0), .c1(c1), .c2(c2), .c3(c3), .c4(c4), .c5(c5));
endmodule

module somabits (
  input  Cin,
  input  A,
  input  B,
  output S,
  output Cout
);

  wire and_1_out, xor_1_out, xor_2_out;

  ExactlyOne xor_1 (.out(xor_1_out), .in0(Cin), .in1(A), .in2(B));
  and and_1 (and_1_out, Cin, A, B);
  ExactlyOne xor_2 (.out(xor_2_out), .in0(Cin), .in1(A), .in2(B));
  or or_1 (S, xor_1_out, and_1_out);
  or or_2 (Cout, and_1_out, xor_2_out);

  // Notes on the sheet:
  //   somabits - Somador bit a bit
endmodule

module somador (
  input  OP,
  input  [7:0] A,
  input  [7:0] B,
  output [7:0] S,
  output CS,
  output SS
);

  wire DIG0_cout, DIG1_cout, DIG2_cout, DIG3_cout, DIG4_cout, DIG5_cout, DIG6_cout, DIG7_cout, xor_1_out,
       xor_2_out, xor_3_out, xor_4_out, xor_5_out, xor_6_out, xor_7_out, xor_8_out;

  xor xor_1 (xor_1_out, B[0], OP);
  xor xor_2 (xor_2_out, B[1], OP);
  xor xor_3 (xor_3_out, B[2], OP);
  xor xor_4 (xor_4_out, B[3], OP);
  xor xor_5 (xor_5_out, B[4], OP);
  xor xor_6 (xor_6_out, B[5], OP);
  xor xor_7 (xor_7_out, B[6], OP);
  xor xor_8 (xor_8_out, B[7], OP);
  somabits DIG0 (.Cin(OP), .A(A[0]), .B(xor_1_out), .S(S[0]), .Cout(DIG0_cout));
  somabits DIG1 (.Cin(DIG0_cout), .A(A[1]), .B(xor_2_out), .S(S[1]), .Cout(DIG1_cout));
  somabits DIG2 (.Cin(DIG1_cout), .A(A[2]), .B(xor_3_out), .S(S[2]), .Cout(DIG2_cout));
  somabits DIG3 (.Cin(DIG2_cout), .A(A[3]), .B(xor_4_out), .S(S[3]), .Cout(DIG3_cout));
  somabits DIG4 (.Cin(DIG3_cout), .A(A[4]), .B(xor_5_out), .S(S[4]), .Cout(DIG4_cout));
  somabits DIG5 (.Cin(DIG4_cout), .A(A[5]), .B(xor_6_out), .S(S[5]), .Cout(DIG5_cout));
  somabits DIG6 (.Cin(DIG5_cout), .A(A[6]), .B(xor_7_out), .S(S[6]), .Cout(DIG6_cout));
  somabits DIG7 (.Cin(DIG6_cout), .A(A[7]), .B(xor_8_out), .S(S[7]), .Cout(DIG7_cout));
  xor xor_9 (SS, DIG7_cout, OP);
  xor xor_10 (CS, DIG6_cout, DIG7_cout);

  // Notes on the sheet:
  //   8 bits
  //   Circuito somador
  //   overflow
endmodule

module comparabits (
  input  A,
  input  B,
  output c0,
  output c1,
  output c2,
  output c3
);

  wire xor_1_out;

  xor xor_1 (xor_1_out, A, B);
  not not_1 (c3, A);
  and and_1 (c0, A, xor_1_out);
  and and_2 (c1, xor_1_out, B);
  not not_2 (c2, xor_1_out);

  // Notes on the sheet:
  //   comparabit - comparador bit a bit
endmodule

module comparador (
  input  [7:0] A,
  input  [7:0] B,
  output c0,
  output c1,
  output c2,
  output c3,
  output c4,
  output c5
);

  wire and_2_out, and_3_out, and_4_out, and_5_out, and_6_out, and_7_out, and_8_out, and_9_out, and_10_out,
       and_11_out, and_12_out, and_13_out, and_14_out, and_15_out, and_17_out, and_18_out, and_19_out,
       and_20_out, and_21_out, and_22_out, and_23_out, and_24_out, and_25_out, and_26_out, comparabits_1_c0,
       comparabits_1_c1, comparabits_1_c2, comparabits_1_c3, comparabits_2_c0, comparabits_2_c1,
       comparabits_2_c2, comparabits_2_c3, comparabits_3_c0, comparabits_3_c1, comparabits_3_c2,
       comparabits_3_c3, comparabits_4_c0, comparabits_4_c1, comparabits_4_c2, comparabits_4_c3,
       comparabits_5_c0, comparabits_5_c1, comparabits_5_c2, comparabits_5_c3, comparabits_6_c0,
       comparabits_6_c1, comparabits_6_c2, comparabits_6_c3, comparabits_7_c0, comparabits_7_c1,
       comparabits_7_c2, comparabits_7_c3, comparabits_8_c0, comparabits_8_c1, comparabits_8_c2,
       comparabits_8_c3, xor_1_out;

  xor xor_1 (xor_1_out, A[7], B[7]);
  comparabits comparabits_1 (
    .A(A[0]), .B(B[0]), .c0(comparabits_1_c0), .c1(comparabits_1_c1), .c2(comparabits_1_c2),
    .c3(comparabits_1_c3));
  comparabits comparabits_2 (
    .A(A[1]), .B(B[1]), .c0(comparabits_2_c0), .c1(comparabits_2_c1), .c2(comparabits_2_c2),
    .c3(comparabits_2_c3));
  comparabits comparabits_3 (
    .A(A[2]), .B(B[2]), .c0(comparabits_3_c0), .c1(comparabits_3_c1), .c2(comparabits_3_c2),
    .c3(comparabits_3_c3));
  comparabits comparabits_4 (
    .A(A[3]), .B(B[3]), .c0(comparabits_4_c0), .c1(comparabits_4_c1), .c2(comparabits_4_c2),
    .c3(comparabits_4_c3));
  comparabits comparabits_5 (
    .A(A[4]), .B(B[4]), .c0(comparabits_5_c0), .c1(comparabits_5_c1), .c2(comparabits_5_c2),
    .c3(comparabits_5_c3));
  comparabits comparabits_6 (
    .A(A[5]), .B(B[5]), .c0(comparabits_6_c0), .c1(comparabits_6_c1), .c2(comparabits_6_c2),
    .c3(comparabits_6_c3));
  comparabits comparabits_7 (
    .A(A[6]), .B(B[6]), .c0(comparabits_7_c0), .c1(comparabits_7_c1), .c2(comparabits_7_c2),
    .c3(comparabits_7_c3));
  comparabits comparabits_8 (
    .A(A[7]), .B(B[7]), .c0(comparabits_8_c0), .c1(comparabits_8_c1), .c2(comparabits_8_c2),
    .c3(comparabits_8_c3));
  and and_1 (c3, comparabits_1_c3, comparabits_2_c3, comparabits_3_c3, comparabits_4_c3, comparabits_5_c3, comparabits_6_c3, comparabits_7_c3, comparabits_8_c3);
  and and_2 (and_2_out, comparabits_1_c0, and_17_out);
  and and_3 (and_3_out, comparabits_1_c1, and_17_out);
  and and_4 (and_4_out, comparabits_2_c0, and_18_out);
  and and_5 (and_5_out, comparabits_2_c1, and_18_out);
  and and_6 (and_6_out, comparabits_3_c0, and_19_out);
  and and_7 (and_7_out, comparabits_3_c1, and_19_out);
  and and_8 (and_8_out, comparabits_4_c0, and_20_out);
  and and_9 (and_9_out, comparabits_4_c1, and_20_out);
  and and_10 (and_10_out, comparabits_5_c0, and_21_out);
  and and_11 (and_11_out, comparabits_5_c1, and_21_out);
  and and_12 (and_12_out, comparabits_6_c0, and_22_out);
  and and_13 (and_13_out, comparabits_6_c1, and_22_out);
  and and_14 (and_14_out, comparabits_7_c0, comparabits_8_c2);
  and and_15 (and_15_out, comparabits_7_c1, comparabits_8_c2);
  and and_16 (c2, comparabits_1_c2, and_17_out);
  and and_17 (and_17_out, comparabits_2_c2, and_18_out);
  and and_18 (and_18_out, comparabits_3_c2, and_19_out);
  and and_19 (and_19_out, comparabits_4_c2, and_20_out);
  and and_20 (and_20_out, comparabits_5_c2, and_21_out);
  and and_21 (and_21_out, comparabits_6_c2, and_22_out);
  and and_22 (and_22_out, comparabits_7_c2, comparabits_8_c2);
  and and_23 (and_23_out, xor_1_out, ~A[7]);  // AND_Gate
  and and_24 (and_24_out, xor_1_out, ~B[7]);  // AND_Gate
  or or_1 (c0, and_2_out, and_4_out, and_6_out, and_8_out, and_10_out, and_12_out, and_14_out, comparabits_8_c0);
  or or_2 (c1, and_3_out, and_5_out, and_7_out, and_9_out, and_11_out, and_13_out, and_15_out, comparabits_8_c1);
  and and_25 (and_25_out, c0, ~xor_1_out);  // AND_Gate
  and and_26 (and_26_out, c1, ~xor_1_out);  // AND_Gate
  or or_3 (c4, and_25_out, and_23_out);
  or or_4 (c5, and_26_out, and_24_out);
endmodule
